// Logisim project Add16.circ as structural Verilog: 1 circuit, main circuit main
module main (
  input  [5:0] a_Add16,
  input  [5:0] b_Add16,
  output [5:0] out_Add16,
  output carry_Add16
);

  wire adder_1_cout, adder_2_cout, adder_3_cout, adder_4_cout, adder_5_cout;

  Adder #(.width(1)) adder_1 (.a(a_Add16[0]), .b(b_Add16[0]), .out(out_Add16[0]), .cout(adder_1_cout));  // open: cin
  Adder #(.width(1)) adder_2 (
    .a(a_Add16[1]), .b(b_Add16[1]), .out(out_Add16[1]), .cin(adder_1_cout), .cout(adder_2_cout));
  Adder #(.width(1)) adder_3 (
    .a(a_Add16[2]), .b(b_Add16[2]), .out(out_Add16[2]), .cin(adder_2_cout), .cout(adder_3_cout));
  Adder #(.width(1)) adder_4 (
    .a(a_Add16[3]), .b(b_Add16[3]), .out(out_Add16[3]), .cin(adder_3_cout), .cout(adder_4_cout));
  Adder #(.width(1)) adder_5 (
    .a(a_Add16[4]), .b(b_Add16[4]), .out(out_Add16[4]), .cin(adder_4_cout), .cout(adder_5_cout));
  Adder #(.width(1)) adder_6 (
    .a(a_Add16[5]), .b(b_Add16[5]), .out(out_Add16[5]), .cin(adder_5_cout), .cout(carry_Add16));
endmodule
