// Logisim project DMuxNWay.circ as structural Verilog: 1 circuit, main circuit main
module main (
  input  in_DMux4Way,
  input  [1:0] sel_DMux4Way,
  input  in_DMux8Way,
  input  [2:0] sel_DMux8Way,
  output a_DMux4Way,
  output b_DMux4Way,
  output c_DMux4Way,
  output d_DMux4Way,
  output a_DMux8Way,
  output b_DMux8Way,
  output c_DMux8Way,
  output d_DMux8Way,
  output e_DMux8Way,
  output f_DMux8Way,
  output g_DMux8Way,
  output h_DMux8Way
);

  wire demultiplexer_1_out0, demultiplexer_1_out1, demultiplexer_4_out0, demultiplexer_4_out1,
       demultiplexer_5_out0, demultiplexer_5_out1, demultiplexer_6_out0, demultiplexer_6_out1;

  Demultiplexer demultiplexer_1 (
    .out0(demultiplexer_1_out0), .out1(demultiplexer_1_out1), .in(in_DMux4Way), .sel(sel_DMux4Way[1]));
  Demultiplexer demultiplexer_2 (
    .out0(a_DMux4Way), .out1(b_DMux4Way), .in(demultiplexer_1_out0), .sel(sel_DMux4Way[0]));
  Demultiplexer demultiplexer_3 (
    .out0(c_DMux4Way), .out1(d_DMux4Way), .in(demultiplexer_1_out1), .sel(sel_DMux4Way[0]));
  Demultiplexer demultiplexer_4 (
    .out0(demultiplexer_4_out0), .out1(demultiplexer_4_out1), .in(in_DMux8Way), .sel(sel_DMux8Way[2]));
  Demultiplexer demultiplexer_5 (
    .out0(demultiplexer_5_out0), .out1(demultiplexer_5_out1), .in(demultiplexer_4_out0), .sel(sel_DMux8Way[1]));
  Demultiplexer demultiplexer_6 (
    .out0(demultiplexer_6_out0), .out1(demultiplexer_6_out1), .in(demultiplexer_4_out1), .sel(sel_DMux8Way[1]));
  Demultiplexer demultiplexer_7 (
    .out0(a_DMux8Way), .out1(b_DMux8Way), .in(demultiplexer_5_out0), .sel(sel_DMux8Way[0]));
  Demultiplexer demultiplexer_8 (
    .out0(c_DMux8Way), .out1(d_DMux8Way), .in(demultiplexer_5_out1), .sel(sel_DMux8Way[0]));
  Demultiplexer demultiplexer_9 (
    .out0(e_DMux8Way), .out1(f_DMux8Way), .in(demultiplexer_6_out0), .sel(sel_DMux8Way[0]));
  Demultiplexer demultiplexer_10 (
    .out0(g_DMux8Way), .out1(h_DMux8Way), .in(demultiplexer_6_out1), .sel(sel_DMux8Way[0]));
endmodule
