// Logisim project HalfFullAdder.circ as structural Verilog: 1 circuit, main circuit main
module main (
  input  a_HalfAdder,
  input  b_HalfAdder,
  input  a_FullAdder,
  input  b_FullAdder,
  input  c_FullAdder,
  output sum_HalfAdder,
  output carry_HalfAdder,
  output sum_FullAdder,
  output carry_Fulladder
);

  wire and_2_out, and_3_out, xor_2_out;

  xor xor_1 (sum_HalfAdder, a_HalfAdder, b_HalfAdder);
  and and_1 (carry_HalfAdder, a_HalfAdder, b_HalfAdder);
  xor xor_2 (xor_2_out, a_FullAdder, b_FullAdder);
  and and_2 (and_2_out, a_FullAdder, b_FullAdder);
  and and_3 (and_3_out, xor_2_out, c_FullAdder);
  xor xor_3 (sum_FullAdder, xor_2_out, c_FullAdder);
  or or_1 (carry_Fulladder, and_3_out, and_2_out);
endmodule
