// Logisim project MuxNWay16.circ as structural Verilog: 1 circuit, main circuit main
module main (
  input  [15:0] a_Mux4Way16,
  input  [15:0] b_Mux4Way16,
  input  [15:0] c_Mux4Way16,
  input  [15:0] d_Mux4Way16,
  input  [1:0] sel_Mux4Way16,
  input  [15:0] a_Mux8Way16,
  input  [15:0] b_Mux8Way16,
  input  [15:0] c_Mux8Way16,
  input  [15:0] d_Mux8Way16,
  input  [15:0] e_Mux8Way16,
  input  [15:0] f_Mux8Way16,
  input  [15:0] g_Mux8Way16,
  input  [15:0] h_Mux8Way16,
  input  [2:0] sel_Mux8Way16,
  output [15:0] out_Mux4Way16,
  output [15:0] out_Mux8Way16
);

  wire [15:0] multiplexer_1_out, multiplexer_2_out, multiplexer_3_out, multiplexer_4_out, multiplexer_5_out,
       multiplexer_6_out, multiplexer_8_out, multiplexer_10_out;

  Multiplexer #(.width(16)) multiplexer_1 (
    .in0(a_Mux4Way16), .in1(b_Mux4Way16), .out(multiplexer_1_out), .sel(sel_Mux4Way16[1]));
  Multiplexer #(.width(16)) multiplexer_2 (
    .in0(c_Mux4Way16), .in1(d_Mux4Way16), .out(multiplexer_2_out), .sel(sel_Mux4Way16[1]));
  Multiplexer #(.width(16)) multiplexer_3 (
    .in0(a_Mux8Way16), .in1(b_Mux8Way16), .out(multiplexer_3_out), .sel(sel_Mux8Way16[2]));
  Multiplexer #(.width(16)) multiplexer_4 (
    .in0(c_Mux8Way16), .in1(d_Mux8Way16), .out(multiplexer_4_out), .sel(sel_Mux8Way16[2]));
  Multiplexer #(.width(16)) multiplexer_5 (
    .in0(e_Mux8Way16), .in1(f_Mux8Way16), .out(multiplexer_5_out), .sel(sel_Mux8Way16[2]));
  Multiplexer #(.width(16)) multiplexer_6 (
    .in0(g_Mux8Way16), .in1(h_Mux8Way16), .out(multiplexer_6_out), .sel(sel_Mux8Way16[2]));
  Multiplexer #(.width(16)) multiplexer_7 (
    .in0(multiplexer_1_out), .in1(multiplexer_2_out), .out(out_Mux4Way16), .sel(sel_Mux4Way16[0]));
  Multiplexer #(.width(16)) multiplexer_8 (
    .in0(multiplexer_3_out), .in1(multiplexer_4_out), .out(multiplexer_8_out), .sel(sel_Mux8Way16[1]));
  Multiplexer #(.width(16)) multiplexer_9 (
    .in0(multiplexer_8_out), .in1(multiplexer_10_out), .out(out_Mux8Way16), .sel(sel_Mux8Way16[0]));
  Multiplexer #(.width(16)) multiplexer_10 (
    .in0(multiplexer_5_out), .in1(multiplexer_6_out), .out(multiplexer_10_out), .sel(sel_Mux8Way16[1]));
endmodule
