// Logisim project ALU.circ as structural Verilog: 1 circuit, main circuit main
module main (
  input  zx,
  input  nx,
  input  zy,
  input  ny,
  input  f,
  input  no,
  input  [15:0] x_ALU,
  input  [15:0] y_ALU,
  output [15:0] out_ALU,
  output zr,
  output ng
);

  wire not_1_out, not_2_out, or_1_out;
  wire [15:0] adder_1_out, and_1_out, and_2_out, and_3_out, bit_extender_1_out, bit_extender_2_out,
       multiplexer_1_out, multiplexer_2_out, multiplexer_3_out, not_3_out, not_4_out, not_5_out;

  not not_1 (not_1_out, zx);
  not not_2 (not_2_out, zy);
  assign bit_extender_1_out = {{15{not_1_out}}, not_1_out};  // Bit_Extender bit_extender_1
  assign and_1_out = bit_extender_1_out & x_ALU;  // AND_Gate and_1, 16 bits wide
  assign bit_extender_2_out = {{15{not_2_out}}, not_2_out};  // Bit_Extender bit_extender_2
  assign and_2_out = bit_extender_2_out & y_ALU;  // AND_Gate and_2, 16 bits wide
  assign not_3_out = ~and_1_out;  // NOT_Gate not_3, 16 bits wide
  assign not_4_out = ~and_2_out;  // NOT_Gate not_4, 16 bits wide
  Multiplexer #(.width(16)) multiplexer_1 (.in0(and_1_out), .in1(not_3_out), .out(multiplexer_1_out), .sel(nx));
  Multiplexer #(.width(16)) multiplexer_2 (.in0(and_2_out), .in1(not_4_out), .out(multiplexer_2_out), .sel(ny));
  assign and_3_out = multiplexer_1_out & multiplexer_2_out;  // AND_Gate and_3, 16 bits wide
  Adder #(.width(16)) adder_1 (.a(multiplexer_1_out), .b(multiplexer_2_out), .out(adder_1_out));  // open: cin, cout
  Multiplexer #(.width(16)) multiplexer_3 (.in0(and_3_out), .in1(adder_1_out), .out(multiplexer_3_out), .sel(f));
  Multiplexer #(.width(16)) multiplexer_4 (
    .in0(multiplexer_3_out), .in1(not_5_out), .out({ng, out_ALU[14:0]}), .sel(no));
  assign not_5_out = ~multiplexer_3_out;  // NOT_Gate not_5, 16 bits wide
  or or_1 (or_1_out, ng, out_ALU[14], out_ALU[13], out_ALU[12], out_ALU[11], out_ALU[10], out_ALU[9], out_ALU[8], out_ALU[7], out_ALU[6], out_ALU[5], out_ALU[4], out_ALU[3], out_ALU[2], out_ALU[1], out_ALU[0]);
  not not_6 (zr, or_1_out);

  assign out_ALU[15] = ng;

  // Notes on the sheet:
  //   x-y
endmodule
