// Logisim project Bit.circ as structural Verilog: 1 circuit, main circuit main
module main (
  input  load,
  input  in_Bit,
  output out_Bit
);

  wire clock_1_out, multiplexer_1_out;

  Clock #(.phaseOffset(1)) clock_1 (.out(clock_1_out));
  Multiplexer multiplexer_1 (.in0(out_Bit), .in1(in_Bit), .out(multiplexer_1_out), .sel(load));
  D_Flip_Flop d_ff_1 (.D(multiplexer_1_out), .clk(clock_1_out), .Q(out_Bit));  // open: Qn, preset, reset
endmodule
