// Logisim project Register.circ as structural Verilog: 1 circuit, main circuit main
module main (
  input  load,
  input  [7:0] in_Register,
  output [7:0] out_Register
);

  wire clock_1_out;

  Clock clock_1 (.out(clock_1_out));
  Register #(.width(1)) register_1 (
    .D(in_Register[0]), .en(load), .clk(clock_1_out), .Q(out_Register[0]));  // open: clr
  Register #(.width(1)) register_2 (
    .D(in_Register[1]), .en(load), .clk(clock_1_out), .Q(out_Register[1]));  // open: clr
  Register #(.width(1)) register_3 (
    .D(in_Register[2]), .en(load), .clk(clock_1_out), .Q(out_Register[2]));  // open: clr
  Register #(.width(1)) register_4 (
    .D(in_Register[3]), .en(load), .clk(clock_1_out), .Q(out_Register[3]));  // open: clr
  Register #(.width(1)) register_5 (
    .D(in_Register[4]), .en(load), .clk(clock_1_out), .Q(out_Register[4]));  // open: clr
  Register #(.width(1)) register_6 (
    .D(in_Register[5]), .en(load), .clk(clock_1_out), .Q(out_Register[5]));  // open: clr
  Register #(.width(1)) register_7 (
    .D(in_Register[6]), .en(load), .clk(clock_1_out), .Q(out_Register[6]));  // open: clr
  Register #(.width(1)) register_8 (
    .D(in_Register[7]), .en(load), .clk(clock_1_out), .Q(out_Register[7]));  // open: clr
endmodule
