// Logisim project Invite.circ as structural Verilog: 1 circuit, main circuit main
module main (
  input  in_1,
  input  in_2,
  input  in_3,
  input  [7:0] in_4,
  input  [7:0] in_5,
  input  [7:0] in_6,
  output out_7,
  output [7:0] out_8
);

  wire or_1_out;
  wire [7:0] or_2_out;

  or or_1 (or_1_out, in_1, in_2);
  assign or_2_out = in_4 | in_5;  // OR_Gate or_2, 8 bits wide
  and and_1 (out_7, or_1_out, in_3);
  assign out_8 = or_2_out & in_6;  // AND_Gate and_2, 8 bits wide
endmodule
