// Logisim project Basic.circ as structural Verilog: 1 circuit, main circuit main
module main (
  input  in_Not,
  input  a_And,
  input  b_And,
  input  a_Or,
  input  b_Or,
  input  a_Xor,
  input  b_Xor,
  output out_Not,
  output out_And,
  output out_Or,
  output out_Xor
);

  wire nand_2_out, nand_4_out, nand_5_out, nand_6_out, not_1_out, not_2_out, not_3_out, not_4_out;

  not not_1 (not_1_out, a_Or);
  not not_2 (not_2_out, b_Or);
  not not_3 (not_3_out, a_Xor);
  not not_4 (not_4_out, b_Xor);
  nand nand_1 (out_Not, in_Not, in_Not);
  nand nand_2 (nand_2_out, a_And, b_And);
  not not_5 (out_And, nand_2_out);
  nand nand_3 (out_Or, not_1_out, not_2_out);
  nand nand_4 (nand_4_out, a_Xor, b_Xor);
  nand nand_5 (nand_5_out, not_3_out, not_4_out);
  nand nand_6 (nand_6_out, nand_4_out, nand_5_out);
  not not_6 (out_Xor, nand_6_out);
endmodule
