// Logisim project Basic16.circ as structural Verilog: 1 circuit, main circuit main
module main (
  input  [15:0] a_And16,
  input  [15:0] b_And16,
  input  [15:0] in_Not16,
  input  [15:0] a_Xor16,
  input  [15:0] b_Xor16,
  input  [15:0] a_Or16,
  input  [15:0] b_Or16,
  output [15:0] out_And16,
  output [15:0] out_Not16,
  output [15:0] out_Xor16,
  output [15:0] out_Or16
);

  wire nand_33_out, nand_34_out, nand_35_out, nand_36_out, nand_37_out, nand_38_out, nand_39_out,
       nand_40_out, nand_41_out, nand_42_out, nand_43_out, nand_44_out, nand_45_out, nand_46_out,
       nand_47_out, nand_48_out, nand_49_out, nand_50_out, nand_51_out, nand_52_out, nand_53_out,
       nand_54_out, nand_55_out, nand_56_out, nand_57_out, nand_58_out, nand_59_out, nand_60_out,
       nand_61_out, nand_62_out, nand_63_out, nand_64_out, nand_65_out, nand_66_out, nand_67_out,
       nand_68_out, nand_69_out, nand_70_out, nand_71_out, nand_72_out, nand_73_out, nand_74_out,
       nand_75_out, nand_76_out, nand_77_out, nand_78_out, nand_79_out, nand_80_out, nand_81_out,
       nand_82_out, nand_83_out, nand_84_out, nand_85_out, nand_86_out, nand_87_out, nand_88_out,
       nand_89_out, nand_90_out, nand_91_out, nand_92_out, nand_93_out, nand_94_out, nand_95_out,
       nand_96_out, not_1_out, not_2_out, not_3_out, not_4_out, not_5_out, not_6_out, not_7_out, not_8_out,
       not_9_out, not_10_out, not_11_out, not_12_out, not_13_out, not_14_out, not_15_out, not_16_out,
       not_17_out, not_18_out, not_19_out, not_20_out, not_21_out, not_22_out, not_23_out, not_24_out,
       not_25_out, not_26_out, not_27_out, not_28_out, not_29_out, not_30_out, not_31_out, not_32_out,
       not_49_out, not_50_out, not_51_out, not_52_out, not_53_out, not_54_out, not_55_out, not_56_out,
       not_57_out, not_58_out, not_59_out, not_60_out, not_61_out, not_62_out, not_63_out, not_64_out,
       not_65_out, not_66_out, not_67_out, not_68_out, not_69_out, not_70_out, not_71_out, not_72_out,
       not_73_out, not_74_out, not_75_out, not_76_out, not_77_out, not_78_out, not_79_out, not_80_out;

  not not_1 (not_1_out, a_Or16[0]);
  not not_2 (not_2_out, b_Or16[0]);
  not not_3 (not_3_out, a_Or16[1]);
  not not_4 (not_4_out, b_Or16[1]);
  not not_5 (not_5_out, a_Or16[2]);
  not not_6 (not_6_out, b_Or16[2]);
  not not_7 (not_7_out, a_Or16[3]);
  not not_8 (not_8_out, b_Or16[3]);
  not not_9 (not_9_out, a_Or16[4]);
  not not_10 (not_10_out, b_Or16[4]);
  not not_11 (not_11_out, a_Or16[5]);
  not not_12 (not_12_out, b_Or16[5]);
  not not_13 (not_13_out, a_Or16[6]);
  not not_14 (not_14_out, b_Or16[6]);
  not not_15 (not_15_out, a_Or16[7]);
  not not_16 (not_16_out, b_Or16[7]);
  not not_17 (not_17_out, a_Or16[8]);
  not not_18 (not_18_out, b_Or16[8]);
  not not_19 (not_19_out, a_Or16[9]);
  not not_20 (not_20_out, b_Or16[9]);
  not not_21 (not_21_out, a_Or16[10]);
  not not_22 (not_22_out, b_Or16[10]);
  not not_23 (not_23_out, a_Or16[11]);
  not not_24 (not_24_out, b_Or16[11]);
  not not_25 (not_25_out, a_Or16[12]);
  not not_26 (not_26_out, b_Or16[12]);
  not not_27 (not_27_out, a_Or16[13]);
  not not_28 (not_28_out, b_Or16[13]);
  not not_29 (not_29_out, a_Or16[14]);
  not not_30 (not_30_out, b_Or16[14]);
  not not_31 (not_31_out, a_Or16[15]);
  not not_32 (not_32_out, b_Or16[15]);
  nand nand_1 (out_Not16[0], in_Not16[0], in_Not16[0]);
  nand nand_2 (out_Not16[1], in_Not16[1], in_Not16[1]);
  nand nand_3 (out_Not16[2], in_Not16[2], in_Not16[2]);
  nand nand_4 (out_Not16[3], in_Not16[3], in_Not16[3]);
  nand nand_5 (out_Not16[4], in_Not16[4], in_Not16[4]);
  nand nand_6 (out_Not16[5], in_Not16[5], in_Not16[5]);
  nand nand_7 (out_Not16[6], in_Not16[6], in_Not16[6]);
  nand nand_8 (out_Not16[7], in_Not16[7], in_Not16[7]);
  nand nand_9 (out_Not16[8], in_Not16[8], in_Not16[8]);
  nand nand_10 (out_Not16[9], in_Not16[9], in_Not16[9]);
  nand nand_11 (out_Not16[10], in_Not16[10], in_Not16[10]);
  nand nand_12 (out_Not16[11], in_Not16[11], in_Not16[11]);
  nand nand_13 (out_Not16[12], in_Not16[12], in_Not16[12]);
  nand nand_14 (out_Not16[13], in_Not16[13], in_Not16[13]);
  nand nand_15 (out_Not16[14], in_Not16[14], in_Not16[14]);
  nand nand_16 (out_Not16[15], in_Not16[15], in_Not16[15]);
  nand nand_17 (out_Or16[0], not_1_out, not_2_out);
  nand nand_18 (out_Or16[1], not_3_out, not_4_out);
  nand nand_19 (out_Or16[2], not_5_out, not_6_out);
  nand nand_20 (out_Or16[3], not_7_out, not_8_out);
  nand nand_21 (out_Or16[4], not_9_out, not_10_out);
  nand nand_22 (out_Or16[5], not_11_out, not_12_out);
  nand nand_23 (out_Or16[6], not_13_out, not_14_out);
  nand nand_24 (out_Or16[7], not_15_out, not_16_out);
  nand nand_25 (out_Or16[8], not_17_out, not_18_out);
  nand nand_26 (out_Or16[9], not_19_out, not_20_out);
  nand nand_27 (out_Or16[10], not_21_out, not_22_out);
  nand nand_28 (out_Or16[11], not_23_out, not_24_out);
  nand nand_29 (out_Or16[12], not_25_out, not_26_out);
  nand nand_30 (out_Or16[13], not_27_out, not_28_out);
  nand nand_31 (out_Or16[14], not_29_out, not_30_out);
  nand nand_32 (out_Or16[15], not_31_out, not_32_out);
  nand nand_33 (nand_33_out, a_And16[0], b_And16[0]);
  not not_33 (out_And16[0], nand_33_out);
  nand nand_34 (nand_34_out, a_And16[1], b_And16[1]);
  not not_34 (out_And16[1], nand_34_out);
  nand nand_35 (nand_35_out, a_And16[2], b_And16[2]);
  not not_35 (out_And16[2], nand_35_out);
  nand nand_36 (nand_36_out, a_And16[3], b_And16[3]);
  not not_36 (out_And16[3], nand_36_out);
  nand nand_37 (nand_37_out, a_And16[4], b_And16[4]);
  not not_37 (out_And16[4], nand_37_out);
  nand nand_38 (nand_38_out, a_And16[5], b_And16[5]);
  not not_38 (out_And16[5], nand_38_out);
  nand nand_39 (nand_39_out, a_And16[6], b_And16[6]);
  not not_39 (out_And16[6], nand_39_out);
  nand nand_40 (nand_40_out, a_And16[7], b_And16[7]);
  not not_40 (out_And16[7], nand_40_out);
  nand nand_41 (nand_41_out, a_And16[8], b_And16[8]);
  not not_41 (out_And16[8], nand_41_out);
  nand nand_42 (nand_42_out, a_And16[9], b_And16[9]);
  not not_42 (out_And16[9], nand_42_out);
  nand nand_43 (nand_43_out, a_And16[10], b_And16[10]);
  not not_43 (out_And16[10], nand_43_out);
  nand nand_44 (nand_44_out, a_And16[11], b_And16[11]);
  not not_44 (out_And16[11], nand_44_out);
  nand nand_45 (nand_45_out, a_And16[12], b_And16[12]);
  not not_45 (out_And16[12], nand_45_out);
  nand nand_46 (nand_46_out, a_And16[13], b_And16[13]);
  not not_46 (out_And16[13], nand_46_out);
  nand nand_47 (nand_47_out, a_And16[14], b_And16[14]);
  not not_47 (out_And16[14], nand_47_out);
  nand nand_48 (nand_48_out, a_And16[15], b_And16[15]);
  not not_48 (out_And16[15], nand_48_out);
  nand nand_49 (nand_49_out, a_Xor16[0], b_Xor16[0]);
  not not_49 (not_49_out, a_Xor16[0]);
  nand nand_50 (nand_50_out, not_49_out, not_50_out);
  not not_50 (not_50_out, b_Xor16[0]);
  nand nand_51 (nand_51_out, a_Xor16[1], b_Xor16[1]);
  not not_51 (not_51_out, a_Xor16[1]);
  nand nand_52 (nand_52_out, not_51_out, not_52_out);
  not not_52 (not_52_out, b_Xor16[1]);
  nand nand_53 (nand_53_out, a_Xor16[2], b_Xor16[2]);
  not not_53 (not_53_out, a_Xor16[2]);
  nand nand_54 (nand_54_out, not_53_out, not_54_out);
  not not_54 (not_54_out, b_Xor16[2]);
  nand nand_55 (nand_55_out, a_Xor16[3], b_Xor16[3]);
  not not_55 (not_55_out, a_Xor16[3]);
  nand nand_56 (nand_56_out, not_55_out, not_56_out);
  not not_56 (not_56_out, b_Xor16[3]);
  nand nand_57 (nand_57_out, a_Xor16[4], b_Xor16[4]);
  not not_57 (not_57_out, a_Xor16[4]);
  nand nand_58 (nand_58_out, not_57_out, not_58_out);
  not not_58 (not_58_out, b_Xor16[4]);
  nand nand_59 (nand_59_out, a_Xor16[5], b_Xor16[5]);
  not not_59 (not_59_out, a_Xor16[5]);
  nand nand_60 (nand_60_out, not_59_out, not_60_out);
  not not_60 (not_60_out, b_Xor16[5]);
  nand nand_61 (nand_61_out, a_Xor16[6], b_Xor16[6]);
  not not_61 (not_61_out, a_Xor16[6]);
  nand nand_62 (nand_62_out, not_61_out, not_62_out);
  not not_62 (not_62_out, b_Xor16[6]);
  nand nand_63 (nand_63_out, a_Xor16[7], b_Xor16[7]);
  not not_63 (not_63_out, a_Xor16[7]);
  nand nand_64 (nand_64_out, not_63_out, not_64_out);
  not not_64 (not_64_out, b_Xor16[7]);
  nand nand_65 (nand_65_out, a_Xor16[8], b_Xor16[8]);
  not not_65 (not_65_out, a_Xor16[8]);
  nand nand_66 (nand_66_out, not_65_out, not_66_out);
  not not_66 (not_66_out, b_Xor16[8]);
  nand nand_67 (nand_67_out, a_Xor16[9], b_Xor16[9]);
  not not_67 (not_67_out, a_Xor16[9]);
  nand nand_68 (nand_68_out, not_67_out, not_68_out);
  not not_68 (not_68_out, b_Xor16[9]);
  nand nand_69 (nand_69_out, a_Xor16[10], b_Xor16[10]);
  not not_69 (not_69_out, a_Xor16[10]);
  nand nand_70 (nand_70_out, not_69_out, not_70_out);
  not not_70 (not_70_out, b_Xor16[10]);
  nand nand_71 (nand_71_out, a_Xor16[11], b_Xor16[11]);
  not not_71 (not_71_out, a_Xor16[11]);
  nand nand_72 (nand_72_out, not_71_out, not_72_out);
  not not_72 (not_72_out, b_Xor16[11]);
  nand nand_73 (nand_73_out, a_Xor16[12], b_Xor16[12]);
  not not_73 (not_73_out, a_Xor16[12]);
  nand nand_74 (nand_74_out, not_73_out, not_74_out);
  not not_74 (not_74_out, b_Xor16[12]);
  nand nand_75 (nand_75_out, a_Xor16[13], b_Xor16[13]);
  not not_75 (not_75_out, a_Xor16[13]);
  nand nand_76 (nand_76_out, not_75_out, not_76_out);
  not not_76 (not_76_out, b_Xor16[13]);
  nand nand_77 (nand_77_out, a_Xor16[14], b_Xor16[14]);
  not not_77 (not_77_out, a_Xor16[14]);
  nand nand_78 (nand_78_out, not_77_out, not_78_out);
  not not_78 (not_78_out, b_Xor16[14]);
  nand nand_79 (nand_79_out, a_Xor16[15], b_Xor16[15]);
  not not_79 (not_79_out, a_Xor16[15]);
  nand nand_80 (nand_80_out, not_79_out, not_80_out);
  not not_80 (not_80_out, b_Xor16[15]);
  nand nand_81 (nand_81_out, nand_49_out, nand_50_out);
  nand nand_82 (nand_82_out, nand_51_out, nand_52_out);
  nand nand_83 (nand_83_out, nand_53_out, nand_54_out);
  nand nand_84 (nand_84_out, nand_55_out, nand_56_out);
  nand nand_85 (nand_85_out, nand_57_out, nand_58_out);
  nand nand_86 (nand_86_out, nand_59_out, nand_60_out);
  nand nand_87 (nand_87_out, nand_61_out, nand_62_out);
  nand nand_88 (nand_88_out, nand_63_out, nand_64_out);
  nand nand_89 (nand_89_out, nand_65_out, nand_66_out);
  nand nand_90 (nand_90_out, nand_67_out, nand_68_out);
  nand nand_91 (nand_91_out, nand_69_out, nand_70_out);
  nand nand_92 (nand_92_out, nand_71_out, nand_72_out);
  nand nand_93 (nand_93_out, nand_73_out, nand_74_out);
  nand nand_94 (nand_94_out, nand_75_out, nand_76_out);
  nand nand_95 (nand_95_out, nand_77_out, nand_78_out);
  nand nand_96 (nand_96_out, nand_79_out, nand_80_out);
  not not_81 (out_Xor16[0], nand_81_out);
  not not_82 (out_Xor16[1], nand_82_out);
  not not_83 (out_Xor16[2], nand_83_out);
  not not_84 (out_Xor16[3], nand_84_out);
  not not_85 (out_Xor16[4], nand_85_out);
  not not_86 (out_Xor16[5], nand_86_out);
  not not_87 (out_Xor16[6], nand_87_out);
  not not_88 (out_Xor16[7], nand_88_out);
  not not_89 (out_Xor16[8], nand_89_out);
  not not_90 (out_Xor16[9], nand_90_out);
  not not_91 (out_Xor16[10], nand_91_out);
  not not_92 (out_Xor16[11], nand_92_out);
  not not_93 (out_Xor16[12], nand_93_out);
  not not_94 (out_Xor16[13], nand_94_out);
  not not_95 (out_Xor16[14], nand_95_out);
  not not_96 (out_Xor16[15], nand_96_out);
endmodule
