// Logisim project DMux.circ as structural Verilog: 1 circuit, main circuit main
module main (
  input  in_DMux,
  input  sel,
  input  [15:0] in_DMux16,
  input  sel_DMux16,
  output a_DMux,
  output b_DMux,
  output [15:0] a_16_DMux16,
  output [15:0] b_DMux16
);

  wire not_1_out;
  wire [15:0] bit_extender_1_out, not_2_out;

  assign bit_extender_1_out = {{15{sel_DMux16}}, sel_DMux16};  // Bit_Extender bit_extender_1
  not not_1 (not_1_out, sel);
  assign not_2_out = ~bit_extender_1_out;  // NOT_Gate not_2, 16 bits wide
  and and_1 (a_DMux, in_DMux, not_1_out);
  and and_2 (b_DMux, in_DMux, sel);
  assign a_16_DMux16 = in_DMux16 & not_2_out;  // AND_Gate and_3, 16 bits wide
  assign b_DMux16 = in_DMux16 & bit_extender_1_out;  // AND_Gate and_4, 16 bits wide
endmodule
