// Logisim project Mux.circ as structural Verilog: 1 circuit, main circuit main
module main (
  input  a_Mux,
  input  sel_Mux,
  input  b_Mux,
  input  [15:0] a_Mux16,
  input  sel_Mux16,
  input  [15:0] b_Mux16,
  output out_Mux,
  output [15:0] out_Mux16
);

  wire and_1_out, and_2_out, not_1_out;
  wire [15:0] and_3_out, and_4_out, bit_extender_1_out, not_2_out;

  assign bit_extender_1_out = {{15{sel_Mux16}}, sel_Mux16};  // Bit_Extender bit_extender_1
  and and_1 (and_1_out, a_Mux, not_1_out);
  not not_1 (not_1_out, sel_Mux);
  and and_2 (and_2_out, sel_Mux, b_Mux);
  assign and_3_out = a_Mux16 & not_2_out;  // AND_Gate and_3, 16 bits wide
  assign not_2_out = ~bit_extender_1_out;  // NOT_Gate not_2, 16 bits wide
  assign and_4_out = bit_extender_1_out & b_Mux16;  // AND_Gate and_4, 16 bits wide
  or or_1 (out_Mux, and_1_out, and_2_out);
  assign out_Mux16 = and_3_out | and_4_out;  // OR_Gate or_2, 16 bits wide
endmodule
